// Logisim project cpu.circ as structural Verilog: 19 circuits, main circuit cpu
module mab (
  input  [7:0] ampa,
  input  cccc,
  input  cc,
  input  [7:0] start,
  input  [2:0] sel,
  output [7:0] nmpa
);

  wire [7:0] adder_1_out, and_1_out, and_2_out, bit_extender_1_out, bit_extender_2_out;

  assign bit_extender_1_out = {{7{cccc}}, cccc};  // Bit_Extender bit_extender_1
  assign bit_extender_2_out = {{7{cc}}, cc};  // Bit_Extender bit_extender_2
  Adder adder_1 (.a(ampa), .b(8'h1), .out(adder_1_out));  // open: cin, cout
  assign and_1_out = adder_1_out & bit_extender_1_out;  // AND_Gate and_1, 8 bits wide
  assign and_2_out = adder_1_out & bit_extender_2_out;  // AND_Gate and_2, 8 bits wide
  Multiplexer #(.select(3), .width(8)) multiplexer_1 (
    .in0(adder_1_out), .in1({8{1'b0}}), .in2(and_1_out), .in3(and_2_out), .in4(start), .out(nmpa), .sel(sel));  // open: in5, in6, in7
endmodule

module SW (
  input  tick,
  input  rst,
  input  [3:0] flags,
  input  [3:0] opno,
  output [31:0] MPSW,
  output write,
  output [2:0] sel
);

  wire bedingung_1_bedingung_out;
  wire [7:0] mab_1_nmpa, register_1_q, SATR_data;

  ROM #(.addrWidth(6)) SATR (.addr({2'b00, opno}), .data(SATR_data));
  bedingung bedingung_1 (
    .ZF(flags[1]), .CF(flags[0]), .OvF(flags[3]), .SF(flags[2]), .Bedingung_Out(bedingung_1_bedingung_out));  // open: cccc
  Register register_1 (.D(mab_1_nmpa), .clk(tick), .Q(register_1_q), .clr(rst));  // open: en
  mab mab_1 (
    .ampa(register_1_q), .cccc(bedingung_1_bedingung_out), .cc(bedingung_1_bedingung_out), .start(SATR_data),
    .sel({1'b0, opno[3:2]}), .nmpa(mab_1_nmpa));
  ROM #(.dataWidth(32)) rom_1 (.addr(register_1_q), .data(MPSW));

  assign sel = {1'b0, opno[3:2]};
  assign write = 1'b0;

  // Notes on the sheet:
  //   contents of rom_1 (hex, n*v repeats v):
  //   ffffffff 16*0 ffffffff 32*0 fffdff
endmodule

module OFD (
  input  VorzeichenOp1,
  input  VorzeichenOp2,
  input  Ergebnis,
  input  sub,
  output Overflow
);

  wire and_1_out, and_2_out, and_3_out, and_4_out, not_1_out, not_2_out, not_3_out, not_4_out;

  not not_1 (not_1_out, VorzeichenOp1);
  not not_2 (not_2_out, VorzeichenOp2);
  not not_3 (not_3_out, Ergebnis);
  not not_4 (not_4_out, sub);
  and and_1 (and_1_out, not_1_out, not_2_out, Ergebnis, not_4_out);
  and and_2 (and_2_out, not_1_out, VorzeichenOp2, Ergebnis, sub);
  and and_3 (and_3_out, VorzeichenOp1, not_2_out, not_3_out, Ergebnis);
  and and_4 (and_4_out, VorzeichenOp1, VorzeichenOp2, not_3_out, not_4_out);
  or or_1 (Overflow, and_1_out, and_2_out, and_3_out, and_4_out);

  // Notes on the sheet:
  //   op1
  //   erg
  //   op2
  //   sub
  //   op1'
  //   op2'
  //   erg'
  //   sub'
endmodule

module ADD (
  input  [7:0] OP1,
  input  [7:0] OP2,
  input  sub,
  input  casc,
  input  keepc,
  input  carry_in,
  output carry_out,
  output [7:0] Ergebnis,
  output overflow
);

  wire adder_1_cout, multiplexer_1_out;
  wire [7:0] inv_1_datenwort_out;

  INV inv_1 (.Steuereingang(sub), .Datenwort(OP2), .Datenwort_Out(inv_1_datenwort_out));
  Multiplexer multiplexer_1 (.in0(carry_in), .in1(1'b0), .out(multiplexer_1_out), .sel(sub));
  Adder adder_1 (.a(OP1), .b(inv_1_datenwort_out), .out(Ergebnis), .cin(multiplexer_1_out), .cout(adder_1_cout));
  Multiplexer multiplexer_2 (.in0(adder_1_cout), .in1(carry_in), .out(carry_out), .sel(keepc));
  OFD ofd_1 (.VorzeichenOp1(OP1[7]), .VorzeichenOp2(OP2[7]), .Ergebnis(Ergebnis[7]), .sub(sub), .Overflow(overflow));
endmodule

module INV (
  input  Steuereingang,
  input  [7:0] Datenwort,
  output [7:0] Datenwort_Out
);

  wire [7:0] adder_1_out, xor_1_out;

  xor xor_1 (xor_1_out[0], Steuereingang, Datenwort[0]);
  xor xor_2 (xor_1_out[1], Steuereingang, Datenwort[1]);
  xor xor_3 (xor_1_out[2], Steuereingang, Datenwort[2]);
  xor xor_4 (xor_1_out[3], Steuereingang, Datenwort[3]);
  xor xor_5 (xor_1_out[4], Steuereingang, Datenwort[4]);
  xor xor_6 (xor_1_out[5], Steuereingang, Datenwort[5]);
  xor xor_7 (xor_1_out[6], Steuereingang, Datenwort[6]);
  xor xor_8 (xor_1_out[7], Steuereingang, Datenwort[7]);
  Adder adder_1 (.a(xor_1_out), .b(8'h1), .out(adder_1_out));  // open: cin, cout
  Multiplexer #(.width(8)) multiplexer_1 (.in0(xor_1_out), .in1(adder_1_out), .out(Datenwort_Out), .sel(Steuereingang));
endmodule

module ALU (
  input  [3:0] opn,
  input  [7:0] OP1,
  input  [7:0] OP2,
  input  carry_in,
  output [7:0] Ergebnis,
  output Zero,
  output Carry_out,
  output Overflow
);

  wire add_1_carry_out, add_1_overflow, and_1_out, and_2_out, decoder_1_out0, decoder_1_out1, decoder_1_out2,
       decoder_1_out3, decoder_1_out4, decoder_1_out5, multiplexer_2_out, or_1_out, or_2_out, or_3_out,
       sre_1_carry_out;
  wire [2:0] bit_extender_1_out;
  wire [7:0] add_1_ergebnis, nand_1_out, sre_1_datenwort_out;

  Bit_Extender #(.in_width(4), .out_width(3), .\type ("zero")) bit_extender_1 (.in(opn), .out(bit_extender_1_out));
  and and_1 (and_1_out, bit_extender_1_out[0], ~bit_extender_1_out[1], ~bit_extender_1_out[2]);  // AND_Gate
  and and_2 (and_2_out, bit_extender_1_out[0], bit_extender_1_out[1], ~bit_extender_1_out[2]);  // AND_Gate
  or or_1 (or_1_out, and_1_out, and_2_out);
  assign nand_1_out = ~(OP1 & OP2);  // NAND_Gate nand_1, 8 bits wide
  ADD add_1 (
    .OP1(OP1), .OP2(OP2), .sub(or_1_out), .casc(bit_extender_1_out[1]), .carry_in(carry_in),
    .carry_out(add_1_carry_out), .Ergebnis(add_1_ergebnis), .overflow(add_1_overflow));  // open: keepc
  SRE sre_1 (
    .Datenwort_in(OP1), .Carry_In(carry_in), .Zahler_Auswahl(OP2), .Datenwort_Out(sre_1_datenwort_out),
    .Carry_Out(sre_1_carry_out));
  Multiplexer #(.select(3), .width(8)) multiplexer_1 (
    .in0(add_1_ergebnis), .in1(add_1_ergebnis), .in2(add_1_ergebnis), .in3(add_1_ergebnis), .in4(nand_1_out),
    .in5(sre_1_datenwort_out), .out(Ergebnis), .sel(bit_extender_1_out));  // open: in6, in7
  Decoder #(.select(3)) decoder_1 (
    .out0(decoder_1_out0), .out1(decoder_1_out1), .out2(decoder_1_out2), .out3(decoder_1_out3),
    .out4(decoder_1_out4), .out5(decoder_1_out5), .sel(bit_extender_1_out));  // open: out6, out7, en
  or or_2 (or_2_out, decoder_1_out0, decoder_1_out1, decoder_1_out2, decoder_1_out3, decoder_1_out5);
  Multiplexer #(.select(3)) multiplexer_2 (
    .in0(add_1_carry_out), .in1(add_1_carry_out), .in2(add_1_carry_out), .in3(add_1_carry_out), .in4(1'b0),
    .in5(sre_1_carry_out), .out(multiplexer_2_out), .sel(bit_extender_1_out));  // open: in6, in7
  or or_3 (or_3_out, decoder_1_out4, or_2_out);
  and and_3 (Zero, ~Ergebnis[7], ~Ergebnis[6], ~Ergebnis[5], ~Ergebnis[4], ~Ergebnis[3], ~Ergebnis[2], ~Ergebnis[1], ~Ergebnis[0]);  // AND_Gate
  and and_4 (Carry_out, or_3_out, multiplexer_2_out);
  and and_5 (Overflow, or_2_out, add_1_overflow);

  // Notes on the sheet:
  //   ADD , SUB , ADC , SBB, NAND , SHIFT
endmodule

module SRE (
  input  [7:0] Datenwort_in,
  input  Carry_In,
  input  [7:0] Zahler_Auswahl,
  output [7:0] Datenwort_Out,
  output Carry_Out
);

  wire [8:0] bit_extender_1_out, shifter_1_out, shifter_2_out, shifter_3_out, shifter_4_out;

  assign bit_extender_1_out = {{1{1'b0}}, Datenwort_in};  // Bit_Extender bit_extender_1
  Shifter #(.width(9)) shifter_1 (.in(bit_extender_1_out), .\dist (Zahler_Auswahl[3:0]), .out(shifter_1_out));
  Shifter #(.shift("lr"), .width(9)) shifter_2 (
    .in(bit_extender_1_out), .\dist (Zahler_Auswahl[3:0]), .out(shifter_2_out));
  Shifter #(.shift("rl"), .width(9)) shifter_3 (
    .in({Carry_In, bit_extender_1_out[7:0]}), .\dist (Zahler_Auswahl[3:0]), .out(shifter_3_out));
  Shifter #(.shift("rr"), .width(9)) shifter_4 (
    .in({Carry_In, bit_extender_1_out[7:0]}), .\dist (Zahler_Auswahl[3:0]), .out(shifter_4_out));
  // Probe on shifter_1_out
  Multiplexer #(.select(2), .width(9)) multiplexer_1 (
    .in0(shifter_1_out), .in1(shifter_2_out), .in2(shifter_3_out), .in3(shifter_4_out),
    .out({Carry_Out, Datenwort_Out}), .sel(Zahler_Auswahl[5:4]));
endmodule

module RW (
  input  [7:0] SP,
  input  [7:0] PP,
  input  write,
  input  [7:0] bbus,
  input  Tock,
  input  [2:0] set_clk,
  input  rst,
  input  [15:0] IP,
  output [7:0] res,
  output [7:0] erg,
  output [3:0] Flags_out,
  output [7:0] OPC_OUT
);

  wire demultiplexer_1_out0, demultiplexer_1_out1, demultiplexer_1_out2, demultiplexer_1_out3,
       demultiplexer_1_out4;
  wire [3:0] alu_1_carry_out;
  wire [7:0] A_q, B_q, C_q, D_q, multiplexer_1_out, multiplexer_2_out, rom_1_data;

  Demultiplexer #(.select(3)) demultiplexer_1 (
    .out0(demultiplexer_1_out0), .out1(demultiplexer_1_out1), .out2(demultiplexer_1_out2),
    .out3(demultiplexer_1_out3), .out4(demultiplexer_1_out4), .in(Tock), .sel(set_clk));  // open: out5, out6, out7
  Register A (.D(bbus), .clk(demultiplexer_1_out0), .Q(A_q), .clr(rst));  // open: en
  Register B (.D(bbus), .clk(demultiplexer_1_out1), .Q(B_q), .clr(rst));  // open: en
  Register C (.D(bbus), .clk(demultiplexer_1_out2), .Q(C_q), .clr(rst));  // open: en
  Register D (.D(bbus), .clk(demultiplexer_1_out3), .Q(D_q), .clr(rst));  // open: en
  Multiplexer #(.select(2), .width(8)) multiplexer_1 (
    .in0(A_q), .in1(B_q), .in2(C_q), .in3(D_q), .out(multiplexer_1_out), .sel(OPC_OUT[5:4]));
  Multiplexer #(.select(2), .width(8)) multiplexer_2 (
    .in0(A_q), .in1(B_q), .in2(C_q), .in3(D_q), .out(multiplexer_2_out), .sel(OPC_OUT[7:6]));
  ROM #(.addrWidth(16)) rom_1 (.addr(IP), .data(rom_1_data));
  ALU alu_1 (
    .opn(OPC_OUT[3:0]), .OP1(multiplexer_1_out), .OP2(multiplexer_2_out), .Ergebnis(erg),
    .Zero(alu_1_carry_out[1]), .Carry_out(alu_1_carry_out[0]), .Overflow(alu_1_carry_out[3]));  // open: carry_in
  RAM #(.addrWidth(16), .enables("line")) ram_1 (
    .addr({PP, SP}), .we(write), .clk(demultiplexer_1_out4), .din(erg), .dout(res));
  Register #(.width(4)) Flags (
    .D({alu_1_carry_out[3], erg[7], alu_1_carry_out[1:0]}), .clk(demultiplexer_1_out4), .Q(Flags_out),
    .clr(rst));  // open: en
  Register OPC (.D(rom_1_data), .clk(demultiplexer_1_out4), .Q(OPC_OUT), .clr(rst));  // open: en
endmodule

module cpu (
  input  rst,
  input  [7:0] in_2,
  input  [7:0] in3,
  input  [7:0] in4,
  output [7:0] out4
);

  wire alu_1_carry_out, alu_1_overflow, alu_1_zero, and_1_out, and_3_out, and_4_out, and_5_out,
       bedingung_1_bedingung_out, clk1, clk2, clkA, clkADRD, clkB, clkC, clkD, clkData, clkFlags, clkIMMH,
       clkIMML, clkIn, clkIP, clkOpc, clkOut, clkSP, cond2, decIP, decSP, demultiplexer_1_out15,
       flags_1_cfout, flags_1_ofout, flags_1_sfout, flags_1_zfout, keyboard_2_avail, not_1_out, opcclk,
       setIP, setSP, stapelzugriff, writeData;
  wire [0:0] cpu_out_1_datenwort_out2;
  wire [1:0] cpu_out_1_datenwort_out1, DSTsel, op1sel, op2sel, SRCsel;
  wire [2:0] mab_steu;
  wire [3:0] ALUopn, dst, dstconst, opc, src, SRCconst;
  wire [5:0] cpu_out_1_datenwort_out1_2;
  wire [6:0] cpu_out_1_datenwort_out2_2, keyboard_1_data, keyboard_2_data, register_8_q;
  wire [7:0] A, B, bit_extender_1_out, C, cpu_out_1_datenwort_out0, D, D_IN, DATA, DBUS, erg, IMMH, IMML,
       Inst, IPH, IPL, mab_1_nmpa, muIP_q, multiplexer_1_out, multiplexer_2_out, register_1_q, register_2_q,
       register_3_q, register_4_q, register_5_q, register_6_q, register_7_q, SAtrans_data, SP,
       spcount_1_spnew, SPdec;
  wire [7:7] register_8_q_2, xor_1_out;
  wire [15:0] ipcount_1_ip, multiplexer_3_out, rampuffer_q;
  wire [15:8] PP_q;
  wire [31:28] mprog_data;

  clk clk_1 (.rst(rst), .CLK2(clk2), .CLK1(clk1));
  _7_Segment_Display u_7_segment_display_1 (
    .g(in_2[6]), .f(in_2[5]), .a(in_2[0]), .b(in_2[1]), .e(in_2[4]), .d(in_2[3]), .c(in_2[2]), .dp(in_2[7]));
  // Probe on op1sel
  Keyboard #(.buflen(256)) keyboard_1 (.data(keyboard_1_data));  // open: clk, re, clr, avail
  Keyboard #(.buflen(256)) keyboard_2 (
    .clk(cpu_out_1_datenwort_out1[0]), .clr(rst), .avail(keyboard_2_avail), .data(keyboard_2_data));  // open: re
  assign bit_extender_1_out = {{7{1'b0}}, keyboard_2_avail};  // Bit_Extender bit_extender_1
  and and_1 (and_1_out, clkIP, clk2);
  // Probe on DBUS
  and and_2 (opcclk, clk2, clkOpc);
  // Probe on keyboard_1_data
  // Probe on keyboard_2_data
  // Probe on DBUS
  // Probe on {1'b0, keyboard_2_data}
  Register u_a (.D(DBUS), .clk(clkA), .Q(A), .clr(rst));  // open: en
  Register u_B (.D(DBUS), .clk(clkB), .Q(B), .clr(rst));  // open: en
  Register u_C (.D(DBUS), .clk(clkC), .Q(C), .clr(rst));  // open: en
  Register u_D (.D(DBUS), .clk(clkD), .Q(D), .clr(rst));  // open: en
  Register PP (.D(DBUS), .Q(PP_q), .clr(rst));  // open: en, clk
  Register u_opc (.D(Inst), .clk(opcclk), .Q({op2sel, op1sel, opc}), .clr(rst));  // open: en
  // Probe on cpu_out_1_datenwort_out0
  CPU_OUT cpu_out_1 (
    .Datenwort_In(DBUS), .port_num(op1sel), .rst(rst), .clk(clkOut),
    .Datenwort_Out0(cpu_out_1_datenwort_out0),
    .Datenwort_Out1({cpu_out_1_datenwort_out1_2, cpu_out_1_datenwort_out1}),
    .Datenwort_Out2({cpu_out_1_datenwort_out2_2, cpu_out_1_datenwort_out2[0]}), .Datenwort_Out3(out4));
  Register u_IMML (.D(DBUS), .clk(clkIMML), .Q(IMML), .clr(rst));  // open: en
  Register u_IMMH (.D(DBUS), .clk(clkIMMH), .Q(IMMH), .clr(rst));  // open: en
  CPU_IN cpu_in_1 (
    .Datenwort_In0({1'b0, keyboard_2_data}), .Datenwort_In1(bit_extender_1_out), .Datenwort_In2(in3),
    .Datenwort_In3(in4), .Port_num(op1sel), .rst(rst), .clk(clkIn), .Datenwort_Out(D_IN));
  // Probe on {cpu_out_1_datenwort_out1_2, cpu_out_1_datenwort_out1}
  // Probe on {cpu_out_1_datenwort_out2_2, cpu_out_1_datenwort_out2[0]}
  // Probe on A
  IPCount ipcount_1 (
    .rst(rst), .loadIP(setIP), .down(decIP), .clk(and_1_out), .IMML(IMML), .IMMH(IMMH), .IPL(IPL), .IPH(IPH),
    .IP(ipcount_1_ip));
  SPcount spcount_1 (
    .rst(rst), .loadSP(setSP), .down(decSP), .clk(clkSP), .SPval(DBUS), .SPnew(spcount_1_spnew));  // open: SPdec
  // Probe on {op2sel, op1sel, opc}
  Multiplexer #(.select(2), .width(8)) multiplexer_1 (
    .in0(A), .in1(B), .in2(C), .in3(D), .out(multiplexer_1_out), .sel(op1sel));
  Multiplexer #(.select(2), .width(8)) multiplexer_2 (
    .in0(A), .in1(B), .in2(C), .in3(D), .out(multiplexer_2_out), .sel(op2sel));
  // Probe on ipcount_1_ip
  ROM #(.addrWidth(16)) instruction_rom (.addr(ipcount_1_ip), .data(Inst));
  Multiplexer #(.width(16)) multiplexer_3 (
    .in0({PP_q, DBUS}), .in1({{8{1'b1}}, spcount_1_spnew}), .out(multiplexer_3_out), .sel(stapelzugriff));
  _7_Segment_Display u_7_segment_display_2 (
    .g(register_1_q[6]), .f(register_1_q[5]), .a(register_1_q[0]), .b(register_1_q[1]), .e(register_1_q[4]),
    .d(register_1_q[3]), .c(register_1_q[2]), .dp(register_1_q[7]));
  Register register_1 (.D(register_2_q), .clk(cpu_out_1_datenwort_out1[1]), .Q(register_1_q), .clr(rst));  // open: en
  and and_3 (and_3_out, clk2, clkFlags);
  Register #(.width(16)) rampuffer (.D(multiplexer_3_out), .clk(clkADRD), .Q(rampuffer_q), .clr(rst));  // open: en
  _7_Segment_Display u_7_segment_display_3 (
    .g(register_2_q[6]), .f(register_2_q[5]), .a(register_2_q[0]), .b(register_2_q[1]), .e(register_2_q[4]),
    .d(register_2_q[3]), .c(register_2_q[2]), .dp(register_2_q[7]));
  Register register_2 (.D(register_3_q), .clk(cpu_out_1_datenwort_out1[1]), .Q(register_2_q), .clr(rst));  // open: en
  // Probe on {cpu_out_1_datenwort_out2_2, cpu_out_1_datenwort_out2[0]}
  // Probe on ALUopn
  Register register_3 (.D(register_4_q), .clk(cpu_out_1_datenwort_out1[1]), .Q(register_3_q), .clr(rst));  // open: en
  flags flags_1 (
    .ZFin(alu_1_zero), .CFin(alu_1_carry_out), .OFin(alu_1_overflow), .SFin(erg[7]), .clkFlags(and_3_out),
    .rst(rst), .ZFout(flags_1_zfout), .CFout(flags_1_cfout), .OFout(flags_1_ofout), .SFout(flags_1_sfout));
  RAM #(.addrWidth(16), .enables("line")) th (
    .addr(rampuffer_q), .we(writeData), .clk(clkData), .din(DBUS), .dout(DATA));
  _7_Segment_Display u_7_segment_display_4 (
    .g(register_3_q[6]), .f(register_3_q[5]), .a(register_3_q[0]), .b(register_3_q[1]), .e(register_3_q[4]),
    .d(register_3_q[3]), .c(register_3_q[2]), .dp(register_3_q[7]));
  ALU alu_1 (
    .opn(ALUopn), .OP1(multiplexer_1_out), .OP2(multiplexer_2_out), .carry_in(flags_1_cfout), .Ergebnis(erg),
    .Zero(alu_1_zero), .Carry_out(alu_1_carry_out), .Overflow(alu_1_overflow));
  _7_Segment_Display u_7_segment_display_5 (
    .g(register_4_q[6]), .f(register_4_q[5]), .a(register_4_q[0]), .b(register_4_q[1]), .e(register_4_q[4]),
    .d(register_4_q[3]), .c(register_4_q[2]), .dp(register_4_q[7]));
  Register register_4 (.D(register_5_q), .clk(cpu_out_1_datenwort_out1[1]), .Q(register_4_q), .clr(rst));  // open: en
  _7_Segment_Display u_7_segment_display_6 (
    .g(register_5_q[6]), .f(register_5_q[5]), .a(register_5_q[0]), .b(register_5_q[1]), .e(register_5_q[4]),
    .d(register_5_q[3]), .c(register_5_q[2]), .dp(register_5_q[7]));
  Register register_5 (.D(register_6_q), .clk(cpu_out_1_datenwort_out1[1]), .Q(register_5_q), .clr(rst));  // open: en
  _7_Segment_Display u_7_segment_display_7 (
    .g(register_6_q[6]), .f(register_6_q[5]), .a(register_6_q[0]), .b(register_6_q[1]), .e(register_6_q[4]),
    .d(register_6_q[3]), .c(register_6_q[2]), .dp(register_6_q[7]));
  Register register_6 (.D(register_7_q), .clk(cpu_out_1_datenwort_out1[1]), .Q(register_6_q), .clr(rst));  // open: en
  // Probe on {op2sel, op1sel}
  // Probe on Inst[3:0]
  // Probe on Inst[7:4]
  // Probe on Inst
  Register register_7 (
    .D({xor_1_out[7], register_8_q}), .clk(cpu_out_1_datenwort_out1[1]), .Q(register_7_q), .clr(rst));  // open: en
  xor xor_1 (xor_1_out[7], register_8_q_2[7], cpu_out_1_datenwort_out2[0]);
  // Probe on opc
  _7_Segment_Display u_7_segment_display_8 (
    .g(register_7_q[6]), .f(register_7_q[5]), .a(register_7_q[0]), .b(register_7_q[1]), .e(register_7_q[4]),
    .d(register_7_q[3]), .c(register_7_q[2]), .dp(register_7_q[7]));
  bedingung bedingung_1 (
    .ZF(flags_1_zfout), .CF(flags_1_cfout), .OvF(flags_1_ofout), .SF(flags_1_sfout), .cccc({op2sel, op1sel}),
    .Bedingung_Out(bedingung_1_bedingung_out));
  _7_Segment_Display u_7_segment_display_9 (
    .g(register_8_q[6]), .f(register_8_q[5]), .a(register_8_q[0]), .b(register_8_q[1]), .e(register_8_q[4]),
    .d(register_8_q[3]), .c(register_8_q[2]), .dp(xor_1_out[7]));
  Register register_8 (
    .D(cpu_out_1_datenwort_out0), .clk(cpu_out_1_datenwort_out1[1]), .Q({register_8_q_2[7], register_8_q}),
    .clr(rst));  // open: en
  ROM #(.dataWidth(32)) mprog (
    .addr(muIP_q),
    .data({mprog_data, mab_steu, ALUopn, clkFlags, decSP, setSP, decIP, setIP, stapelzugriff, clkIP, writeData, clkOpc, SRCsel, DSTsel, dstconst, SRCconst}));
  and and_4 (and_4_out, bedingung_1_bedingung_out, and_5_out);
  and and_5 (and_5_out, ~opc[0], opc[1], ~opc[2], opc[3]);  // AND_Gate
  not not_1 (not_1_out, and_5_out);
  or or_1 (cond2, and_4_out, not_1_out);
  // Probe on {mprog_data, mab_steu, ALUopn, clkFlags, decSP, setSP, decIP, setIP, stapelzugriff, clkIP, writeData, clkOpc, SRCsel, DSTsel, dstconst, SRCconst}
  // Probe on {op2sel, op1sel, opc}
  // Probe on opc[0]
  Demultiplexer #(.select(4)) demultiplexer_1 (
    .out0(clkA), .out1(clkB), .out2(clkC), .out3(clkD), .out4(clkIMML), .out5(clkIMMH), .out6(clkOut),
    .out7(clkIn), .out8(clkData), .out9(clkADRD), .out10(clkSP), .out15(demultiplexer_1_out15), .in(clk2),
    .sel(dst));  // open: out11, out12, out13, out14
  // Probe on muIP_q
  ROM #(.addrWidth(6)) SAtrans (.addr({2'b00, opc}), .data(SAtrans_data));
  // Probe on DSTsel
  // NoConnect on demultiplexer_1_out15
  // Probe on dst
  Multiplexer #(.select(2), .width(4)) multiplexer_4 (
    .in0({2'b00, op1sel}), .in1({2'b00, op2sel}), .in2(dstconst), .in3(4'b1111), .out(dst), .sel(DSTsel));
  Multiplexer #(.select(2), .width(4)) multiplexer_5 (
    .in0({2'b00, op1sel}), .in1({2'b00, op2sel}), .in2(SRCconst), .in3(4'b1111), .out(src), .sel(SRCsel));
  // Probe on SRCsel
  // Probe on dst
  // Probe on src
  // Probe on mab_steu
  Register muIP (.D(mab_1_nmpa), .clk(clk1), .Q(muIP_q), .clr(rst));  // open: en
  // Probe on A
  mab mab_1 (.ampa(muIP_q), .cccc(cond2), .cc(cond2), .start(SAtrans_data), .sel(mab_steu), .nmpa(mab_1_nmpa));
  Multiplexer #(.select(4), .width(8)) multiplexer_6 (
    .in0(A), .in1(B), .in2(C), .in3(D), .in4(erg), .in5(IMML), .in6(IMMH), .in7(SP), .in8(SPdec), .in9(IPL),
    .in10(IPH), .in11(Inst), .in12(DATA), .in13(D_IN), .in15({8{1'b0}}), .out(DBUS), .sel(src));  // open: in14
  // Probe on src
  // Probe on mab_1_nmpa
  // Probe on DBUS

  // Other names for the same wires on the sheet: opc[7:4] = {op2sel, op1sel}; port_num[1:0] = op1sel; cond4 = cond2

  // Notes on the sheet:
  //   Rechenwerk
  //   Instruction
  //   Data Ram
  //   contents of mprog (hex, n*v repeats v):
  //   8005f00 8005100 8105804 8305804 8905804 2b00804 8305f00 290 2002680 690 200080c 6004a4b 2000905 4a5b
  //   4004a4b 2014f00 8005660 e70 200090d
  //   Mikro-Programm-ROM
  //   Steuerwerk
  //   contents of SAtrans (hex, n*v repeats v):
  //   0 1 2 3 4 5 6 7 9 b d 10 11
  //   Start-Adress-Transformations-ROM
endmodule

module bedingung (
  input  ZF,
  input  CF,
  input  OvF,
  input  SF,
  input  [3:0] cccc,
  output Bedingung_Out
);

  wire and_1_out, and_2_out, and_3_out, and_4_out, and_5_out, and_6_out, and_7_out, and_8_out, and_9_out,
       and_10_out, and_11_out, and_12_out, and_13_out, and_14_out, decoder_1_out0, decoder_1_out1,
       decoder_1_out2, decoder_1_out3, decoder_1_out4, decoder_1_out5, decoder_1_out6, decoder_1_out7,
       decoder_1_out8, decoder_1_out9, decoder_1_out10, decoder_1_out11, decoder_1_out12, decoder_1_out13,
       decoder_1_out14, not_1_out, not_2_out, not_3_out, not_4_out, not_5_out, or_1_out, or_2_out, xor_1_out,
       xor_2_out;

  not not_1 (not_1_out, SF);
  not not_2 (not_2_out, CF);
  not not_3 (not_3_out, OvF);
  not not_4 (not_4_out, ZF);
  xor xor_1 (xor_1_out, OvF, SF);
  not not_5 (not_5_out, xor_1_out);
  Decoder #(.select(4)) decoder_1 (
    .out0(decoder_1_out0), .out1(decoder_1_out1), .out2(decoder_1_out2), .out3(decoder_1_out3),
    .out4(decoder_1_out4), .out5(decoder_1_out5), .out6(decoder_1_out6), .out7(decoder_1_out7),
    .out8(decoder_1_out8), .out9(decoder_1_out9), .out10(decoder_1_out10), .out11(decoder_1_out11),
    .out12(decoder_1_out12), .out13(decoder_1_out13), .out14(decoder_1_out14), .sel(cccc));  // open: out15, en
  and and_1 (and_1_out, decoder_1_out2, CF);
  or or_1 (or_1_out, CF, ZF);
  and and_2 (and_2_out, not_4_out, decoder_1_out1);
  and and_3 (and_3_out, or_1_out, decoder_1_out3);
  and and_4 (and_4_out, not_4_out, not_2_out, decoder_1_out4);
  and and_5 (and_5_out, not_2_out, decoder_1_out5);
  xor xor_2 (xor_2_out, OvF, SF);
  and and_6 (and_6_out, xor_2_out, decoder_1_out6);
  or or_2 (or_2_out, xor_2_out, ZF);
  and and_7 (and_7_out, or_2_out, decoder_1_out7);
  and and_8 (and_8_out, not_4_out, not_5_out, decoder_1_out8);
  and and_9 (and_9_out, not_5_out, decoder_1_out9);
  and and_10 (and_10_out, OvF, decoder_1_out10);
  and and_11 (and_11_out, not_3_out, decoder_1_out11);
  and and_12 (and_12_out, SF, decoder_1_out12);
  and and_13 (and_13_out, not_1_out, decoder_1_out13);
  and and_14 (and_14_out, ZF, decoder_1_out14);
  or or_3 (Bedingung_Out, decoder_1_out0, and_2_out, and_1_out, and_3_out, and_4_out, and_5_out, and_6_out, and_7_out, and_8_out, and_9_out, and_10_out, and_11_out, and_12_out, and_13_out, and_14_out);
  // Probe on Bedingung_Out

  // Notes on the sheet:
  //   u ne b be a ae l le g ge o no s ns e x
endmodule

module clk (
  input  rst,
  output CLK2,
  output CLK1
);

  wire clock_1_out, d_ff_1_qn;

  Clock clock_1 (.out(clock_1_out));
  D_Flip_Flop d_ff_1 (.D(d_ff_1_qn), .clk(clock_1_out), .Q(CLK1), .Qn(d_ff_1_qn), .reset(rst));  // open: preset
  and and_1 (CLK2, d_ff_1_qn, ~rst);  // AND_Gate
endmodule

module flags (
  input  ZFin,
  input  CFin,
  input  OFin,
  input  SFin,
  input  clkFlags,
  input  rst,
  output ZFout,
  output CFout,
  output OFout,
  output SFout
);

  Register #(.width(4)) register_1 (
    .D({SFin, OFin, CFin, ZFin}), .clk(clkFlags), .Q({SFout, OFout, CFout, ZFout}), .clr(rst));  // open: en
endmodule

module IPCount (
  input  rst,
  input  loadIP,
  input  down,
  input  clk,
  input  [7:0] IMML,
  input  [7:0] IMMH,
  output [7:0] IPL,
  output [7:0] IPH,
  output [15:0] IP
);

  wire not_1_out;

  Counter #(.max('hffff), .width(16)) counter_1 (
    .clr(rst), .load(loadIP), .up(not_1_out), .clk(clk), .D({IMMH, IMML}), .Q(IP));  // open: count, carry
  not not_1 (not_1_out, down);

  assign IPH = IP[15:8];
  assign IPL = IP[7:0];
endmodule

module SPcount (
  input  rst,
  input  loadSP,
  input  down,
  input  clk,
  input  [7:0] SPval,
  output [7:0] SPnew,
  output [7:0] SPdec
);

  wire not_1_out;

  Counter counter_1 (.clr(rst), .load(loadSP), .up(not_1_out), .clk(clk), .D(SPval), .Q(SPnew));  // open: count, carry
  not not_1 (not_1_out, down);
  Subtractor subtractor_1 (.a(SPnew), .b(8'h1), .out(SPdec));  // open: bin, bout
endmodule

module SSA (
  input  rst
);

  wire button_1_out;
  wire [6:0] keyboard_1_data, ram_1_dout;
  wire [7:0] bit_extender_1_out, register_1_q, register_2_q, register_3_q, register_4_q, register_5_q,
       register_6_q, register_7_q, register_8_q;

  Keyboard #(.buflen(256)) keyboard_1 (.clk(button_1_out), .clr(rst), .data(keyboard_1_data));  // open: re, avail
  Button button_1 (.out(button_1_out));
  // Probe on keyboard_1_data
  RAM #(.addrWidth(7), .dataWidth(7), .enables("line")) ram_1 (
    .addr(keyboard_1_data), .dout(ram_1_dout));  // open: we, clk, din
  _7_Segment_Display u_7_segment_display_1 (
    .g(register_1_q[6]), .f(register_1_q[5]), .a(register_1_q[0]), .b(register_1_q[1]), .e(register_1_q[4]),
    .d(register_1_q[3]), .c(register_1_q[2]), .dp(register_1_q[7]));
  Register register_1 (.D(register_2_q), .clk(button_1_out), .Q(register_1_q), .clr(rst));  // open: en
  _7_Segment_Display u_7_segment_display_2 (
    .g(register_2_q[6]), .f(register_2_q[5]), .a(register_2_q[0]), .b(register_2_q[1]), .e(register_2_q[4]),
    .d(register_2_q[3]), .c(register_2_q[2]), .dp(register_2_q[7]));
  Register register_2 (.D(register_3_q), .clk(button_1_out), .Q(register_2_q), .clr(rst));  // open: en
  Register register_3 (.D(register_4_q), .clk(button_1_out), .Q(register_3_q), .clr(rst));  // open: en
  assign bit_extender_1_out = {{1{1'b0}}, ram_1_dout};  // Bit_Extender bit_extender_1
  _7_Segment_Display u_7_segment_display_3 (
    .g(register_3_q[6]), .f(register_3_q[5]), .a(register_3_q[0]), .b(register_3_q[1]), .e(register_3_q[4]),
    .d(register_3_q[3]), .c(register_3_q[2]), .dp(register_3_q[7]));
  _7_Segment_Display u_7_segment_display_4 (
    .g(register_4_q[6]), .f(register_4_q[5]), .a(register_4_q[0]), .b(register_4_q[1]), .e(register_4_q[4]),
    .d(register_4_q[3]), .c(register_4_q[2]), .dp(register_4_q[7]));
  Register register_4 (.D(register_5_q), .clk(button_1_out), .Q(register_4_q), .clr(rst));  // open: en
  _7_Segment_Display u_7_segment_display_5 (
    .g(register_5_q[6]), .f(register_5_q[5]), .a(register_5_q[0]), .b(register_5_q[1]), .e(register_5_q[4]),
    .d(register_5_q[3]), .c(register_5_q[2]), .dp(register_5_q[7]));
  Register register_5 (.D(register_6_q), .clk(button_1_out), .Q(register_5_q), .clr(rst));  // open: en
  _7_Segment_Display u_7_segment_display_6 (
    .g(register_6_q[6]), .f(register_6_q[5]), .a(register_6_q[0]), .b(register_6_q[1]), .e(register_6_q[4]),
    .d(register_6_q[3]), .c(register_6_q[2]), .dp(register_6_q[7]));
  Register register_6 (.D(register_7_q), .clk(button_1_out), .Q(register_6_q), .clr(rst));  // open: en
  Register register_7 (.D(register_8_q), .clk(button_1_out), .Q(register_7_q), .clr(rst));  // open: en
  _7_Segment_Display u_7_segment_display_7 (
    .g(register_7_q[6]), .f(register_7_q[5]), .a(register_7_q[0]), .b(register_7_q[1]), .e(register_7_q[4]),
    .d(register_7_q[3]), .c(register_7_q[2]), .dp(register_7_q[7]));
  _7_Segment_Display u_7_segment_display_8 (
    .g(register_8_q[6]), .f(register_8_q[5]), .a(register_8_q[0]), .b(register_8_q[1]), .e(register_8_q[4]),
    .d(register_8_q[3]), .c(register_8_q[2]), .dp(register_8_q[7]));
  Register register_8 (.D(bit_extender_1_out), .clk(button_1_out), .Q(register_8_q), .clr(rst));  // open: en
endmodule

module tetris (
);

  Keyboard keyboard_1 ();  // open: clk, re, clr, avail, data
  Random random_1 ();  // open: clr, next, clk, out
  // RGB_Video #(.cursor("No Cursor"), .height(16), .scale(8), .width(16)) rgb_video_1: pin names not known
endmodule

module sor (
  input  [6:0] in_1,
  output out_2
);

  or or_1 (out_2, in_1[0], in_1[1], in_1[2], in_1[3], in_1[4], in_1[5], in_1[6]);
endmodule

module CPU_OUT (
  input  [7:0] Datenwort_In,
  input  [1:0] port_num,
  input  rst,
  input  clk,
  output [7:0] Datenwort_Out0,
  output [7:0] Datenwort_Out1,
  output [7:0] Datenwort_Out2,
  output [7:0] Datenwort_Out3
);

  wire decoder_1_out0, decoder_1_out1, decoder_1_out2, decoder_1_out3;

  Decoder #(.select(2)) decoder_1 (
    .out0(decoder_1_out0), .out1(decoder_1_out1), .out2(decoder_1_out2), .out3(decoder_1_out3), .sel(port_num));  // open: en
  Register register_1 (.D(Datenwort_In), .en(decoder_1_out0), .clk(clk), .Q(Datenwort_Out0), .clr(rst));
  Register register_2 (.D(Datenwort_In), .en(decoder_1_out1), .clk(clk), .Q(Datenwort_Out1), .clr(rst));
  Register register_3 (.D(Datenwort_In), .en(decoder_1_out2), .clk(clk), .Q(Datenwort_Out2), .clr(rst));
  Register register_4 (.D(Datenwort_In), .en(decoder_1_out3), .clk(clk), .Q(Datenwort_Out3), .clr(rst));
endmodule

module CPU_IN (
  input  [7:0] Datenwort_In0,
  input  [7:0] Datenwort_In1,
  input  [7:0] Datenwort_In2,
  input  [7:0] Datenwort_In3,
  input  [1:0] Port_num,
  input  rst,
  input  clk,
  output [7:0] Datenwort_Out
);

  wire [7:0] multiplexer_1_out;

  Multiplexer #(.select(2), .width(8)) multiplexer_1 (
    .in0(Datenwort_In0), .in1(Datenwort_In1), .in2(Datenwort_In2), .in3(Datenwort_In3),
    .out(multiplexer_1_out), .sel(Port_num));
  Register register_1 (.D(multiplexer_1_out), .clk(clk), .Q(Datenwort_Out), .clr(rst));  // open: en
endmodule
